// Logisim project projetpdf.circ as structural Verilog: 7 circuits, main circuit main
module main (
  input  in_1,
  output [15:0] out_2,
  output [15:0] AAAAAAAAAA,
  output [15:0] DDDDD,
  output [15:0] out_5,
  output [15:0] out_6,
  output [15:0] output_mem
);

  wire clock_1_out, cpu_1_writem;
  wire [15:0] cpu_1_out_6;

  Clock clock_1 (.out(clock_1_out));
  RAM #(.addrWidth(16), .dataWidth(16), .databus("bibus")) ram_1 (
    .addr(out_6), .we(cpu_1_writem), .oe(1'b1), .clk(clock_1_out), .din(cpu_1_out_6), .dout(output_mem));
  CPU cpu_1 (
    .in_1(out_2), .in_2(output_mem), .reset(in_1), .writeM(cpu_1_writem), .out_5(out_5), .out_6(cpu_1_out_6),
    .out_8(out_6), .A(AAAAAAAAAA), .DDDD(DDDDD));
  ROM #(.addrWidth(16), .dataWidth(16)) rom_1 (.addr(out_5), .data(out_2));

  // Notes on the sheet:
  //   address
  //   contents of rom_1 (hex, n*v repeats v):
  //   1 efc8 2 efc8 3 ec10 0 e308 0 fc00 fc90 e390 e320 fc00 fc10 ede0 ede0 e308 eca0 fc00 fc10 ede0 fc00
  //   f088 0 fc00 fdc8 8 e007
endmodule

module ALU (
  input  zx,
  input  [15:0] X,
  input  nx,
  input  zy,
  input  f,
  input  no,
  input  [15:0] Y,
  input  ny,
  output [15:0] OUT,
  output zr,
  output ng
);

  wire [15:0] adder_1_out, and_1_out, multiplexer_1_out, multiplexer_2_out, multiplexer_3_out,
       multiplexer_4_out, multiplexer_5_out, not_1_out, not_2_out, not_3_out, not_5_out;

  Multiplexer #(.width(16), .enable("false")) multiplexer_1 (
    .in0(X), .in1({16{1'b0}}), .out(multiplexer_1_out), .sel(zx));
  Multiplexer #(.width(16), .enable("false")) multiplexer_2 (
    .in0(Y), .in1({16{1'b0}}), .out(multiplexer_2_out), .sel(zy));
  assign not_1_out = ~multiplexer_2_out;  // NOT_Gate not_1, 16 bits wide
  assign not_2_out = ~multiplexer_1_out;  // NOT_Gate not_2, 16 bits wide
  Multiplexer #(.width(16), .enable("false")) multiplexer_3 (
    .in0(multiplexer_2_out), .in1(not_1_out), .out(multiplexer_3_out), .sel(ny));
  Multiplexer #(.width(16), .enable("false")) multiplexer_4 (
    .in0(multiplexer_1_out), .in1(not_2_out), .out(multiplexer_4_out), .sel(nx));
  assign not_3_out = ~OUT;  // NOT_Gate not_3, 16 bits wide
  Adder #(.width(16)) adder_1 (.a(multiplexer_4_out), .b(multiplexer_3_out), .out(adder_1_out));  // open: cin, cout
  assign and_1_out = multiplexer_4_out & multiplexer_3_out;  // AND_Gate and_1, 16 bits wide
  not not_4 (ng, not_3_out[15]);
  Multiplexer #(.width(16), .enable("false")) multiplexer_5 (
    .in0(and_1_out), .in1(adder_1_out), .out(multiplexer_5_out), .sel(f));
  and and_2 (zr, not_3_out[0], not_3_out[1], not_3_out[2], not_3_out[3], not_3_out[4], not_3_out[5], not_3_out[6], not_3_out[7], not_3_out[8], not_3_out[9], not_3_out[10], not_3_out[11], not_3_out[12], not_3_out[13], not_3_out[14], not_3_out[15]);
  Multiplexer #(.width(16), .enable("false")) multiplexer_6 (
    .in0(multiplexer_5_out), .in1(not_5_out), .out(OUT), .sel(no));
  assign not_5_out = ~multiplexer_5_out;  // NOT_Gate not_5, 16 bits wide
endmodule

module onebitreg (
  input  data,
  input  load1,
  output stored
);

  D_Flip_Flop d_ff_1 (.clk(stored), .D(data), .preset(load1));  // open: Q, Qn, reset
  Multiplexer #(.enable("false")) multiplexer_1 (.in0(stored), .in1(data), .sel(load1));  // open: out
  Clock clock_1 ();  // open: out
endmodule

module \reg  (
  input  in_1,
  input  [15:0] in,
  output [15:0] out_3
);

  onebitreg onebitreg_1 (.stored(out_3[0]), .data(in[0]), .load1(in_1));
  onebitreg onebitreg_2 (.stored(out_3[1]), .data(in[1]), .load1(in_1));
  onebitreg onebitreg_3 (.stored(out_3[2]), .data(in[2]), .load1(in_1));
  onebitreg onebitreg_4 (.stored(out_3[3]), .data(in[3]), .load1(in_1));
  onebitreg onebitreg_5 (.stored(out_3[4]), .data(in[4]), .load1(in_1));
  onebitreg onebitreg_6 (.stored(out_3[5]), .data(in[5]), .load1(in_1));
  onebitreg onebitreg_7 (.stored(out_3[6]), .data(in[6]), .load1(in_1));
  onebitreg onebitreg_8 (.stored(out_3[7]), .data(in[7]), .load1(in_1));
  onebitreg onebitreg_9 (.stored(out_3[8]), .data(in[8]), .load1(in_1));
  onebitreg onebitreg_10 (.stored(out_3[9]), .data(in[9]), .load1(in_1));
  onebitreg onebitreg_11 (.stored(out_3[10]), .data(in[10]), .load1(in_1));
  onebitreg onebitreg_12 (.stored(out_3[11]), .data(in[11]), .load1(in_1));
  onebitreg onebitreg_13 (.stored(out_3[12]), .data(in[12]), .load1(in_1));
  onebitreg onebitreg_14 (.stored(out_3[13]), .data(in[13]), .load1(in_1));
  onebitreg onebitreg_15 (.stored(out_3[14]), .data(in[14]), .load1(in_1));
  onebitreg onebitreg_16 (.stored(out_3[15]), .data(in[15]), .load1(in_1));
endmodule

module RAM8 (
  input  in_1,
  input  [15:0] in_2,
  input  [2:0] in_3,
  output [15:0] out_4,
  output [15:0] out_5,
  output [15:0] out_6,
  output [15:0] out_7,
  output [15:0] out_8,
  output [15:0] out_9,
  output [15:0] out_10,
  output [15:0] out_11
);

  wire demultiplexer_1_out0, demultiplexer_1_out1, demultiplexer_1_out2, demultiplexer_1_out3,
       demultiplexer_1_out4, demultiplexer_1_out5, demultiplexer_1_out6, demultiplexer_1_out7;

  Demultiplexer #(.select(3), .enable("false")) demultiplexer_1 (
    .out0(demultiplexer_1_out0), .out1(demultiplexer_1_out1), .out2(demultiplexer_1_out2),
    .out3(demultiplexer_1_out3), .out4(demultiplexer_1_out4), .out5(demultiplexer_1_out5),
    .out6(demultiplexer_1_out6), .out7(demultiplexer_1_out7), .in(in_1), .sel(in_3));
  \reg  reg_1 (.in(in_2), .in_1(demultiplexer_1_out0), .out_3(out_4));
  \reg  reg_2 (.in(in_2), .in_1(demultiplexer_1_out1), .out_3(out_5));
  \reg  reg_3 (.in(in_2), .in_1(demultiplexer_1_out2), .out_3(out_6));
  \reg  reg_4 (.in(in_2), .in_1(demultiplexer_1_out3), .out_3(out_7));
  \reg  reg_5 (.in(in_2), .in_1(demultiplexer_1_out4), .out_3(out_8));
  \reg  reg_6 (.in(in_2), .in_1(demultiplexer_1_out5), .out_3(out_9));
  \reg  reg_7 (.in(in_2), .in_1(demultiplexer_1_out6), .out_3(out_10));
  \reg  reg_8 (.in(in_2), .in_1(demultiplexer_1_out7), .out_3(out_11));
endmodule

module pc (
  input  load,
  input  reset,
  input  [15:0] in_3,
  input  inc,
  output [15:0] out_5
);

  wire [15:0] alu_1_out, multiplexer_1_out, multiplexer_2_out, multiplexer_3_out;

  Multiplexer #(.width(16), .enable("false")) multiplexer_1 (
    .in0(alu_1_out), .in1(in_3), .out(multiplexer_1_out), .sel(load));
  Multiplexer #(.width(16), .enable("false")) multiplexer_2 (
    .in0(multiplexer_1_out), .in1({16{1'b0}}), .out(multiplexer_2_out), .sel(reset));
  Multiplexer #(.width(16), .enable("false")) multiplexer_3 (
    .in0({16{1'b0}}), .in1(16'h1), .out(multiplexer_3_out), .sel(inc));
  \reg  reg_1 (.in(multiplexer_2_out), .in_1(1'b1), .out_3(out_5));
  ALU alu_1 (
    .X(out_5), .Y(multiplexer_3_out), .OUT(alu_1_out), .zy(1'b0), .zx(1'b0), .ny(1'b0), .nx(1'b0), .f(1'b1),
    .no(1'b0));  // open: zr, ng

  // Notes on the sheet:
  //   signal + 1 si inc
  //   in
endmodule

module CPU (
  input  [15:0] in_1,
  input  [15:0] in_2,
  input  reset,
  output writeM,
  output [15:0] out_5,
  output [15:0] out_6,
  output [15:0] A,
  output [15:0] out_8,
  output [15:0] DDDD
);

  wire alu_1_ng, alu_1_zr, and_1_out, and_2_out, and_3_out, and_4_out, and_5_out, and_6_out, not_1_out,
       not_2_out, not_3_out, or_1_out, or_2_out;
  wire [15:0] multiplexer_1_out, multiplexer_2_out;

  and and_1 (and_1_out, in_1[4], in_1[15]);
  Multiplexer #(.width(16), .enable("false")) multiplexer_1 (
    .in0(A), .in1(in_2), .out(multiplexer_1_out), .sel(in_1[12]));
  \reg  D (.in(out_6), .in_1(and_1_out), .out_3(DDDD));
  ALU alu_1 (
    .X(DDDD), .Y(multiplexer_1_out), .OUT(out_6), .zr(alu_1_zr), .ng(alu_1_ng), .zy(in_1[9]), .zx(in_1[11]),
    .ny(in_1[8]), .nx(in_1[10]), .f(in_1[7]), .no(in_1[6]));
  Multiplexer #(.width(16), .enable("false")) multiplexer_2 (
    .in0(in_1), .in1(out_6), .out(multiplexer_2_out), .sel(in_1[15]));
  not not_1 (not_1_out, alu_1_ng);
  not not_2 (not_2_out, alu_1_zr);
  and and_2 (and_2_out, not_2_out, not_1_out);
  not not_3 (not_3_out, in_1[15]);
  or or_1 (or_1_out, not_3_out, in_1[5]);
  \reg  D_2 (.in(multiplexer_2_out), .in_1(or_1_out), .out_3(A));
  and and_3 (and_3_out, in_1[2], alu_1_ng);
  and and_4 (and_4_out, in_1[0], and_2_out);
  and and_5 (and_5_out, in_1[1], alu_1_zr);
  pc pc_1 (.load(and_6_out), .reset(reset), .in_3(A), .inc(1'b1), .out_5(out_5));
  and and_6 (and_6_out, or_2_out, in_1[15]);
  or or_2 (or_2_out, and_5_out, and_3_out, and_4_out);
  and and_7 (writeM, in_1[3], in_1[15]);

  assign out_8 = A;

  // Notes on the sheet:
  //   A
  //   D
  //   INSTRUCTION
  //   inM
  //   si c'est un 0 on remplit A
  //   AA
  //   pos
  //   ACTIVER INC POUR TESTER
  //   activer options aussi
  //   zr
  //   ng
  //   JUMP HERE
  //   PC
  //   ADDress
  //   OUT
endmodule
